# Fritzing sketch Box wiring (saved by Fritzing 0.9.3b)

parts:
  Arduino1 = Arduino Uno (Rev3)
  J1 = Piezo Speaker [part_number=458-1252-ND]
  LED1 = LED - 3mm [color="Red (633nm)" part_number=67-1106-ND package="3 mm [THT]"]
  J3 = female pin header, 2 pins [form="♀ (female)"]
  J4 = female pin header, 2 pins [form="♀ (female)"]
  J5 = female pin header, 2 pins [form="♀ (female)"]
  J6 = Generic female header - 5 pins [form="♀ (female)" package=THT]
  R1 = Temperature Sensor (Thermistor) [thermistor_type=NTC package=THT]
  R2 = Temperature Sensor (Thermistor) [thermistor_type=NTC package=THT]
  U3 = POT_SWITCH [package=pot_pth_switch]
  U4 = BNC socket [part_number=A97548-ND package=bnc]
  U5 = BNC socket [part_number=A97548-ND package=bnc]
  HLK-PM1 = HLK-PM01
  J7 = Camdenboss CTB0158-2 [part_number=CTB0158-2 package=THT]
  switch1 = Rotary_Switch_12x1
  RELAY1 = CAR RELAY [part_number=NVF4-2 package=THT]
  RELAY2 = CAR RELAY [part_number=NVF4-2 package=THT]
  RELAY3 = CAR RELAY [part_number=NVF4-2 package=THT]
  J8 = Camdenboss CTB0158-2 [part_number=CTB0158-2 package=THT]
  J9 = Power Jack [part_number=SC1937-ND package=power_jack_pth]
  J10 = Power Jack [part_number=SC1937-ND package=power_jack_combo]
  J11 = Power Jack [part_number=SC1937-ND package=power_jack_combo]
  U6 = BNC socket [part_number=A97548-ND package=bnc]
  U7 = BNC socket [package=bnc]
  U8 = BNC socket [part_number=A97548-ND package=bnc]
  U9 = BNC socket [part_number=A97548-ND package=bnc]
  U10 = BNC socket [part_number=A97548-ND package=bnc]
  S1 = Taiway 100-SP-X-T1 SPDT Miniature Toggle Switch [part_number=100-SP-X-T1-0-0-B1-M1 package=THT]
  TRRS1 = Audio Jack (TRRS) 3.5mm [part_number=CP-3536-ND package="RC-5325A [SMD]"]
  JP1 = Header 2 [package=r_sw_th]
  F1 = FUSE [package=fuse_5mm]
  Power_plug1 = Power plug
  JP2 = Header 2 [package=r_sw_th]
  M1 = DC Motor

nets:
  N1: Arduino1.A0, R1.pin_0
  N2: Arduino1.A1, R2.pin_0
  N3: Arduino1.A2, TRRS1.TIP
  N4: Arduino1.A4/SDA, U5.OUT
  N5: Arduino1.A5/SCL, U3.W
  N6: Arduino1.D10_PWM/SS, LED1.anode
  N7: Arduino1.D12/MISO, J1.pin2
  GND: Arduino1.GND, J1.pin1, LED1.cathode, U3.B, U6.GND, U7.GND, S1.COM, TRRS1.SLEEVE
  N8: Arduino1.D2, S1.L1
  N9: Arduino1.D5_PWM, U7.OUT
  N10: Arduino1.D6_PWM, U6.OUT
  N11: Arduino1.5V, U3.SW1
  N12: J3.pin1, U8.GND
  N13: J3.pin2, U8.OUT
  N14: J4.pin1, U9.OUT
  N15: J4.pin2, U9.GND
  N16: J5.pin1, U10.OUT
  N17: J5.pin2, U10.GND
  N18: J6.GND#0, R1.pin_1
  N19: J6.GND#1, U5.GND
  N20: J6.GND#2, U4.GND
  N21: J6.A3, U4.OUT
  N22: J6.GND#4, R2.pin_1
  N23: U3.SW2, U3.A
  N24: HLK-PM1.AC#0, JP1.1, JP2.1
  N25: HLK-PM1.AC#1, Power_plug1.GND, M1.pin_2
  N26: HLK-PM1.-Vo, J7.pin2, RELAY1.86, RELAY2.86, RELAY3.86
  N27: HLK-PM1.+Vo, J7.pin1, switch1.0
  N28: switch1.3, RELAY2.85
  N29: switch1.9, RELAY3.85
  N30: switch1.12, RELAY1.85
  N31: RELAY1.30, RELAY2.30, RELAY3.30, J8.terminal_1
  N32: RELAY1.87, J10.PWR
  N33: RELAY2.87, J11.PWR
  N34: RELAY3.87, J9.PWR
  GND_2: J8.terminal_2, J9.GND, J10.GND, J11.GND
  N35: JP1.2, F1.2
  N36: F1.1, Power_plug1.VCC
  N37: JP2.2, M1.pin_1

notes:
  BLINK
  AC input
  AC fan
  AC-DC converter
  SP4T switch and relays (optional)
  DC input
  LED output
  Cover ICSP with shrink tubing

custom parts:
  Generic female header - 5 pins: Generic female header
  POT_SWITCH: Potentiometer w/ switch.

// code stored in the sketch: Blink.ino
/*
  Blink
  
  Switching a LED on and off
  
  This example is part of the Fritzing Creator Kit: www.fritzing.org/creator-kit.
*/

int led = 13;                   // integer variable led is declared

void setup() {                  // the setup() method is executed only once
  pinMode(led, OUTPUT);         // the led PIN is declared as digital output
}

void loop() {                   // the loop() method is repeated
  digitalWrite(led, HIGH);      // switching on the led 
  delay(1000);                  // stopping the program for 1000 milliseconds
  digitalWrite(led, LOW);       // switching off the led 
  delay(1000);                  // stopping the program for 1000 milliseconds
}
